// Logisim project DADO.circ as structural Verilog: 1 circuit, main circuit main
module main (
);

  wire and_1_out, button_1_out, clock_1_out, decoder_1_out0, decoder_1_out1, decoder_1_out2, decoder_1_out3,
       decoder_1_out4, decoder_1_out5, or_1_out, or_2_out, or_3_out, t_ff_1_q;
  wire [2:0] counter_1_q;

  Button button_1 (.out(button_1_out));
  Counter #(.width(3), .max('h5)) counter_1 (.Q(counter_1_q), .clk(and_1_out));  // open: load, D, count, carry, clr
  and and_1 (and_1_out, t_ff_1_q, clock_1_out);
  T_Flip_Flop t_ff_1 (.clk(button_1_out), .T(1'b1), .Q(t_ff_1_q));  // open: Qn, preset, reset, en
  Clock clock_1 (.out(clock_1_out));
  Decoder #(.select(3)) decoder_1 (
    .out0(decoder_1_out0), .out1(decoder_1_out1), .out2(decoder_1_out2), .out3(decoder_1_out3),
    .out4(decoder_1_out4), .out5(decoder_1_out5), .sel(counter_1_q));  // open: out6, out7, en
  or or_1 (or_1_out, decoder_1_out1, decoder_1_out2, decoder_1_out3, decoder_1_out4, decoder_1_out5);
  or or_2 (or_2_out, decoder_1_out3, decoder_1_out4, decoder_1_out5);
  or or_3 (or_3_out, decoder_1_out0, decoder_1_out2, decoder_1_out4);
  LED led_1 (.in(or_1_out));
  LED led_2 (.in(decoder_1_out5));
  LED led_3 (.in(or_3_out));
  LED led_4 (.in(or_2_out));
  LED led_5 (.in(or_2_out));
  LED led_6 (.in(decoder_1_out5));
  LED led_7 (.in(or_1_out));
endmodule
