// Logisim project Flip-Flop-Toggle2.circ as structural Verilog: 1 circuit, main circuit main
module main (
  input  in_1
);

  wire clock_1_out, t_ff_1_q, t_ff_2_q, t_ff_3_q;

  LED led_1 (.in(clock_1_out));
  Clock clock_1 (.out(clock_1_out));
  LED led_2 (.in(t_ff_1_q));
  T_Flip_Flop t_ff_1 (.clk(clock_1_out), .T(in_1), .Q(t_ff_1_q));  // open: Qn, preset, reset, en
  LED led_3 (.in(t_ff_2_q));
  T_Flip_Flop t_ff_2 (.clk(t_ff_1_q), .T(in_1), .Q(t_ff_2_q));  // open: Qn, preset, reset, en
  LED led_4 (.in(t_ff_3_q));
  T_Flip_Flop t_ff_3 (.clk(t_ff_2_q), .T(in_1), .Q(t_ff_3_q));  // open: Qn, preset, reset, en

  // Notes on the sheet:
  //   f
  //   f / 2
  //   f / 4
  //   f / 8
endmodule
