// Logisim project Flip-FlopJK.circ as structural Verilog: 1 circuit, main circuit main
module main (
  input  in_1,
  input  in_2
);

  wire button_1_out, button_2_out, button_3_out, clock_1_out, j_k_ff_1_q, j_k_ff_1_qn;

  Clock clock_1 (.out(clock_1_out));
  Button button_1 (.out(button_1_out));
  LED led_1 (.in(j_k_ff_1_q));
  J_K_Flip_Flop j_k_ff_1 (
    .J(in_1), .clk(clock_1_out), .K(in_2), .Q(j_k_ff_1_q), .Qn(j_k_ff_1_qn), .preset(button_1_out),
    .en(button_2_out), .reset(button_3_out));
  LED led_2 (.in(j_k_ff_1_qn));
  Button button_2 (.out(button_2_out));
  Button button_3 (.out(button_3_out));
endmodule
