// Logisim project Flip-FlopSR.circ as structural Verilog: 1 circuit, main circuit main
module main (
  input  in_1,
  input  in_2
);

  wire button_1_out, button_2_out, button_3_out, clock_1_out, s_r_ff_1_q, s_r_ff_1_qn;

  Clock clock_1 (.out(clock_1_out));
  Button button_1 (.out(button_1_out));
  LED led_1 (.in(s_r_ff_1_q));
  S_R_Flip_Flop s_r_ff_1 (
    .S(in_1), .clk(clock_1_out), .R(in_2), .Q(s_r_ff_1_q), .Qn(s_r_ff_1_qn), .preset(button_1_out),
    .reset(button_3_out), .en(button_2_out));
  LED led_2 (.in(s_r_ff_1_qn));
  Button button_2 (.out(button_2_out));
  Button button_3 (.out(button_3_out));
endmodule
